# Fritzing sketch obstacle_avoiding_robot (saved by Fritzing 0.9.3b)
breadboards: 2

parts:
  L298N1 = L298N DC motor driver
  hc-sr1 = hc-sr04
  BAT1 = BC9VPC [package=bc9vpc]
  MH-ET_LIVE_ESP32_DEVKIT1 = MH-ET LIVE ESP32 DEVKIT 38 pins
  SERVO1 = Tower Pro SG90 servo [part_number=101246]
  M3 = DC Motor  # not connected
  M4 = DC Motor
  M5 = DC Motor
  M6 = DC Motor

nets:
  N1: L298N1.OUT2, M5.pin_1
  N2: L298N1.OUT3, M6.pin_2
  N3: L298N1.OUT4, M4.pin_1
  12V: L298N1.12V, BAT1.V-, MH-ET_LIVE_ESP32_DEVKIT1.5V, SERVO1.+5V
  GND: L298N1.GND, hc-sr1.GND, BAT1.V+, MH-ET_LIVE_ESP32_DEVKIT1.GND#64, SERVO1.GND
  N4: L298N1.ENA, MH-ET_LIVE_ESP32_DEVKIT1.IO23
  N5: L298N1.ENB, MH-ET_LIVE_ESP32_DEVKIT1.IO5
  N6: L298N1.IN1, MH-ET_LIVE_ESP32_DEVKIT1.IO22
  N7: L298N1.IN2, MH-ET_LIVE_ESP32_DEVKIT1.IO21
  N8: L298N1.IN3, MH-ET_LIVE_ESP32_DEVKIT1.IO19
  N9: L298N1.IN4, MH-ET_LIVE_ESP32_DEVKIT1.IO18
  VCC: hc-sr1.VCC, MH-ET_LIVE_ESP32_DEVKIT1.3V3
  N10: hc-sr1.Trig, MH-ET_LIVE_ESP32_DEVKIT1.IO17
  N11: hc-sr1.Echo, MH-ET_LIVE_ESP32_DEVKIT1.IO16
  N12: MH-ET_LIVE_ESP32_DEVKIT1.IO15, SERVO1.Signal

custom parts:
  L298N DC motor driver: 2x DC motor driver with 78M05 positive voltage regulator (7..35 V) L298N: max 46 V, 2 A Set 5 V Enable jumper to enable 5 V regultor (needed for the L298N) and +5 V output at screw terminal or supply external +5 V at screw terminal Set ENA and/or ENB to +5 V to enable motor permanently or supply ENA and/or ENB with PWM signal IN1 and IN2 set rotation directory for motor A (OUT1/OUT2) IN2 and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
  MH-ET LIVE ESP32 DEVKIT 38 pins: http://mh.nodebb.com/topic/2/mh-et-live-esp32-devkit
  Tower Pro SG90 servo: Original file by John De Cristofaro http://www.adafruit.com/products/1449 Adafruit Feedback Servo (Small) Edited by: e-radionica.com 28/9/2015
